# Fritzing sketch connections (saved by Fritzing 1.0.1rc)
breadboards: 1

parts:
  J1 = STM32 Nucleo boards
  A1 = Waveshare e-Paper HAT [package=THT]
  R1 = Resistor [tolerance=±5% resistance=4.7k package="2010 [SMD]"]
  R2 = Resistor [tolerance=±5% resistance=4.7k package="2010 [SMD]"]
  U1 = VCNL4000 [package=vcnl4000]
  Part1 = Soil Moisture Sensor
  U2 = TMP36 [package=to-92-kit]

nets:
  VCC: J1.3v3, A1.pin_8, R1.Pin_0, R2.Pin_0, U1.VDD, Part1.VCC, U2.VCC
  GND: J1.GND, A1.pin_7, U1.GND, Part1.GND, U2.GND
  N1: J1.PA6, U2.VOUT
  N2: J1.PA7, Part1.SIG
  N3: J1.PB6, R1.Pin_1, U1.SCL
  N4: J1.PA9, A1.pin_3
  N5: J1.PA8, A1.pin_2
  N6: J1.PB10, A1.pin_5
  N7: J1.PA10, A1.pin_4
  N8: J1.PC1, A1.pin_6
  N9: J1.PB7, R2.Pin_1, U1.SDA

custom parts:
  Waveshare e-Paper HAT: .This is a universal driver board for e-Paper raw panels, can be used to drive various SPI interface e-Paper from Waveshare.
